// Logisim project Simulation.circ as structural Verilog: 8 circuits, main circuit main
module main (
  input  [7:0] in_1,
  input  [7:0] in_2,
  input  in_3,
  output out_4
);

  wire bcd_to_7_segment_decoder_1_p1, bcd_to_7_segment_decoder_2_p1, bcd_to_7_segment_decoder_2_p2,
       bcd_to_7_segment_decoder_2_p3, bcd_to_7_segment_decoder_2_p4, bcd_to_7_segment_decoder_2_p6,
       bcd_to_7_segment_decoder_2_p7, bcd_to_7_segment_decoder_2_p8, bcd_to_7_segment_decoder_3_p1,
       bcd_to_7_segment_decoder_3_p2, bcd_to_7_segment_decoder_3_p3, bcd_to_7_segment_decoder_3_p4,
       bcd_to_7_segment_decoder_3_p6, bcd_to_7_segment_decoder_3_p7, bcd_to_7_segment_decoder_3_p8,
       bcd_to_7_segment_decoder_4_p1, bcd_to_7_segment_decoder_4_p2, bcd_to_7_segment_decoder_4_p3,
       bcd_to_7_segment_decoder_4_p4, bcd_to_7_segment_decoder_4_p6, bcd_to_7_segment_decoder_4_p7,
       bcd_to_7_segment_decoder_4_p8, button_1_out, button_2_out, button_3_out, clock_1_out, not_1_out,
       undriven;
  wire [0:0] sign_calculator_1_sign;
  wire [3:0] bcd_to_7_segment_decoder_2_p5, bcd_to_7_segment_decoder_3_p5, bcd_to_7_segment_decoder_4_p5,
       binary_to_bcd_1_d0, binary_to_bcd_1_d1, binary_to_bcd_1_d2, binary_to_bcd_1_d3, binary_to_bcd_1_d4;
  wire [7:0] sign_calculator_1_abs_multiplicand, sign_calculator_1_abs_multiplier;
  wire [15:0] sm_1_result;

  Button button_1 (.out(button_1_out));
  Clock clock_1 (.out(clock_1_out));
  Sign_Calculator sign_calculator_1 (
    .Multiplier(in_1), .Multiplicand(in_2), .ABS_Multiplier(sign_calculator_1_abs_multiplier),
    .Sign(sign_calculator_1_sign[0]), .ABS_Multiplicand(sign_calculator_1_abs_multiplicand));
  SM sm_1 (
    .Reset(button_1_out), .Multiplier(sign_calculator_1_abs_multiplier), .Load(in_3), .clk(clock_1_out),
    .Multiplicand(sign_calculator_1_abs_multiplicand), .Result(sm_1_result), .Done(out_4));
  // BCD_to_7_Segment_decoder bcd_to_7_segment_decoder_1: pin names not known; wires that end beside it: bcd_to_7_segment_decoder_1_p1, {3'b000, sign_calculator_1_sign[0]}
  not not_1 (not_1_out, bcd_to_7_segment_decoder_1_p1);
  _7_Segment_Display u_7_segment_display_1 (.g(not_1_out), .dp(undriven));  // open: f, a, b, e, d, c
  // BCD_to_7_Segment_decoder bcd_to_7_segment_decoder_2: pin names not known; wires that end beside it: bcd_to_7_segment_decoder_2_p1, bcd_to_7_segment_decoder_2_p2, bcd_to_7_segment_decoder_2_p3, bcd_to_7_segment_decoder_2_p4, bcd_to_7_segment_decoder_2_p5, bcd_to_7_segment_decoder_2_p6, bcd_to_7_segment_decoder_2_p7, bcd_to_7_segment_decoder_2_p8
  _7_Segment_Display u_7_segment_display_2 (
    .g(bcd_to_7_segment_decoder_2_p1), .f(bcd_to_7_segment_decoder_2_p3), .a(bcd_to_7_segment_decoder_2_p6),
    .b(bcd_to_7_segment_decoder_2_p8), .e(bcd_to_7_segment_decoder_2_p2), .d(bcd_to_7_segment_decoder_2_p4),
    .c(bcd_to_7_segment_decoder_2_p7), .dp(undriven));
  Binary_to_BCD binary_to_bcd_1 (
    .Binary_IN(sm_1_result), .D4(binary_to_bcd_1_d4), .D3(binary_to_bcd_1_d3), .D2(binary_to_bcd_1_d2),
    .D1(binary_to_bcd_1_d1), .D0(binary_to_bcd_1_d0));
  // BCD_to_7_Segment_decoder bcd_to_7_segment_decoder_3: pin names not known; wires that end beside it: bcd_to_7_segment_decoder_3_p1, bcd_to_7_segment_decoder_3_p2, bcd_to_7_segment_decoder_3_p3, bcd_to_7_segment_decoder_3_p4, bcd_to_7_segment_decoder_3_p5, bcd_to_7_segment_decoder_3_p6, bcd_to_7_segment_decoder_3_p7, bcd_to_7_segment_decoder_3_p8
  _7_Segment_Display u_7_segment_display_3 (
    .g(bcd_to_7_segment_decoder_3_p1), .f(bcd_to_7_segment_decoder_3_p3), .a(bcd_to_7_segment_decoder_3_p6),
    .b(bcd_to_7_segment_decoder_3_p8), .e(bcd_to_7_segment_decoder_3_p2), .d(bcd_to_7_segment_decoder_3_p4),
    .c(bcd_to_7_segment_decoder_3_p7), .dp(undriven));
  Button button_2 (.out(button_2_out));
  Button button_3 (.out(button_3_out));
  // BCD_to_7_Segment_decoder bcd_to_7_segment_decoder_4: pin names not known; wires that end beside it: bcd_to_7_segment_decoder_4_p1, bcd_to_7_segment_decoder_4_p2, bcd_to_7_segment_decoder_4_p3, bcd_to_7_segment_decoder_4_p4, bcd_to_7_segment_decoder_4_p5, bcd_to_7_segment_decoder_4_p6, bcd_to_7_segment_decoder_4_p7, bcd_to_7_segment_decoder_4_p8
  _7_Segment_Display u_7_segment_display_4 (
    .g(bcd_to_7_segment_decoder_4_p1), .f(bcd_to_7_segment_decoder_4_p3), .a(bcd_to_7_segment_decoder_4_p6),
    .b(bcd_to_7_segment_decoder_4_p8), .e(bcd_to_7_segment_decoder_4_p2), .d(bcd_to_7_segment_decoder_4_p4),
    .c(bcd_to_7_segment_decoder_4_p7), .dp(undriven));
  Shift_Register shift_register_1 (
    .BTNR(button_2_out), .Reset(button_1_out), .D4(binary_to_bcd_1_d4), .D3(binary_to_bcd_1_d3),
    .D2(binary_to_bcd_1_d2), .D1(binary_to_bcd_1_d1), .D0(binary_to_bcd_1_d0), .BTNL(button_3_out),
    .clk(clock_1_out), .O2(bcd_to_7_segment_decoder_2_p5), .O1(bcd_to_7_segment_decoder_3_p5),
    .O0(bcd_to_7_segment_decoder_4_p5));
endmodule

module Sign_Calculator (
  input  [7:0] Multiplier,
  input  [7:0] Multiplicand,
  output [7:0] ABS_Multiplier,
  output Sign,
  output [7:0] ABS_Multiplicand
);

  wire [6:0] xor_2_out, xor_4_out;

  xor xor_1 (xor_2_out[1], Multiplier[1], Multiplier[7]);
  xor xor_2 (xor_2_out[0], Multiplier[0], Multiplier[7]);
  xor xor_3 (xor_4_out[1], Multiplicand[1], Multiplicand[7]);
  xor xor_4 (xor_4_out[0], Multiplicand[0], Multiplicand[7]);
  xor xor_5 (xor_2_out[3], Multiplier[3], Multiplier[7]);
  xor xor_6 (xor_2_out[2], Multiplier[2], Multiplier[7]);
  xor xor_7 (xor_4_out[3], Multiplicand[3], Multiplicand[7]);
  xor xor_8 (xor_4_out[2], Multiplicand[2], Multiplicand[7]);
  xor xor_9 (xor_2_out[5], Multiplier[5], Multiplier[7]);
  xor xor_10 (xor_2_out[4], Multiplier[4], Multiplier[7]);
  xor xor_11 (xor_4_out[5], Multiplicand[5], Multiplicand[7]);
  xor xor_12 (xor_4_out[4], Multiplicand[4], Multiplicand[7]);
  xor xor_13 (xor_2_out[6], Multiplier[6], Multiplier[7]);
  Adder adder_1 (.a({8{1'b0}}), .b({1'b0, xor_2_out}), .out(ABS_Multiplier), .cin(Multiplier[7]));  // open: cout
  xor xor_14 (xor_4_out[6], Multiplicand[6], Multiplicand[7]);
  Adder adder_2 (.a({8{1'b0}}), .b({1'b0, xor_4_out}), .out(ABS_Multiplicand), .cin(Multiplicand[7]));  // open: cout
  xor xor_15 (Sign, Multiplier[7], Multiplicand[7]);
endmodule

module Binary_to_BCD (
  input  [15:0] Binary_IN,
  output [3:0] D4,
  output [3:0] D3,
  output [3:0] D2,
  output [3:0] D1,
  output [3:0] D0
);

  wire add_3_if_ge_5_2_out0, add_3_if_ge_5_2_out1, add_3_if_ge_5_2_out2, add_3_if_ge_5_2_out3,
       add_3_if_ge_5_3_out0, add_3_if_ge_5_3_out1, add_3_if_ge_5_3_out2, add_3_if_ge_5_3_out3,
       add_3_if_ge_5_4_out0, add_3_if_ge_5_4_out1, add_3_if_ge_5_4_out2, add_3_if_ge_5_4_out3,
       add_3_if_ge_5_7_out0, add_3_if_ge_5_7_out1, add_3_if_ge_5_7_out2, add_3_if_ge_5_7_out3,
       add_3_if_ge_5_8_out0, add_3_if_ge_5_8_out1, add_3_if_ge_5_8_out2, add_3_if_ge_5_8_out3,
       add_3_if_ge_5_9_out0, add_3_if_ge_5_9_out1, add_3_if_ge_5_9_out2, add_3_if_ge_5_9_out3,
       add_3_if_ge_5_10_out0, add_3_if_ge_5_10_out1, add_3_if_ge_5_10_out2, add_3_if_ge_5_10_out3,
       add_3_if_ge_5_11_out0, add_3_if_ge_5_11_out1, add_3_if_ge_5_11_out2, add_3_if_ge_5_11_out3,
       add_3_if_ge_5_12_out0, add_3_if_ge_5_12_out1, add_3_if_ge_5_12_out2, add_3_if_ge_5_12_out3,
       add_3_if_ge_5_13_out0, add_3_if_ge_5_13_out1, add_3_if_ge_5_13_out2, add_3_if_ge_5_13_out3,
       add_3_if_ge_5_14_out0, add_3_if_ge_5_14_out1, add_3_if_ge_5_14_out2, add_3_if_ge_5_14_out3,
       add_3_if_ge_5_15_out0, add_3_if_ge_5_15_out1, add_3_if_ge_5_15_out2, add_3_if_ge_5_15_out3,
       add_3_if_ge_5_16_out0, add_3_if_ge_5_16_out1, add_3_if_ge_5_16_out2, add_3_if_ge_5_16_out3,
       add_3_if_ge_5_17_out0, add_3_if_ge_5_17_out1, add_3_if_ge_5_17_out2, add_3_if_ge_5_17_out3,
       add_3_if_ge_5_18_out0, add_3_if_ge_5_18_out1, add_3_if_ge_5_18_out2, add_3_if_ge_5_18_out3,
       add_3_if_ge_5_19_out0, add_3_if_ge_5_19_out1, add_3_if_ge_5_19_out2, add_3_if_ge_5_19_out3,
       add_3_if_ge_5_20_out0, add_3_if_ge_5_20_out1, add_3_if_ge_5_20_out2, add_3_if_ge_5_20_out3,
       add_3_if_ge_5_21_out0, add_3_if_ge_5_21_out1, add_3_if_ge_5_21_out2, add_3_if_ge_5_21_out3,
       add_3_if_ge_5_22_out0, add_3_if_ge_5_22_out1, add_3_if_ge_5_22_out2, add_3_if_ge_5_22_out3,
       add_3_if_ge_5_23_out0, add_3_if_ge_5_23_out1, add_3_if_ge_5_23_out2, add_3_if_ge_5_23_out3,
       add_3_if_ge_5_24_out0, add_3_if_ge_5_24_out1, add_3_if_ge_5_24_out2, add_3_if_ge_5_24_out3,
       add_3_if_ge_5_25_out0, add_3_if_ge_5_25_out1, add_3_if_ge_5_25_out2, add_3_if_ge_5_25_out3,
       add_3_if_ge_5_26_out0, add_3_if_ge_5_26_out1, add_3_if_ge_5_26_out2, add_3_if_ge_5_26_out3,
       add_3_if_ge_5_27_out0, add_3_if_ge_5_27_out1, add_3_if_ge_5_27_out2, add_3_if_ge_5_27_out3,
       add_3_if_ge_5_30_out0, add_3_if_ge_5_30_out1, add_3_if_ge_5_30_out2, add_3_if_ge_5_30_out3,
       add_3_if_ge_5_31_out0, add_3_if_ge_5_31_out1, add_3_if_ge_5_31_out2, add_3_if_ge_5_31_out3,
       add_3_if_ge_5_32_out0, add_3_if_ge_5_32_out1, add_3_if_ge_5_32_out2, add_3_if_ge_5_32_out3,
       add_3_if_ge_5_33_out0, add_3_if_ge_5_33_out1, add_3_if_ge_5_33_out2, add_3_if_ge_5_33_out3,
       add_3_if_ge_5_34_out0, add_3_if_ge_5_34_out1, add_3_if_ge_5_34_out2, add_3_if_ge_5_34_out3,
       add_3_if_ge_5_35_out0, add_3_if_ge_5_35_out1, add_3_if_ge_5_35_out2, add_3_if_ge_5_35_out3;

  Add_3_if_GE_5 add_3_if_ge_5_1 (
    .IN3(1'b0), .IN2(add_3_if_ge_5_3_out3), .IN1(add_3_if_ge_5_2_out3), .IN0(add_3_if_ge_5_7_out3),
    .OUT2(D4[3]), .OUT1(D4[2]), .OUT0(D4[1]));  // open: OUT3
  Add_3_if_GE_5 add_3_if_ge_5_2 (
    .IN3(add_3_if_ge_5_3_out2), .IN2(add_3_if_ge_5_3_out1), .IN1(add_3_if_ge_5_3_out0),
    .IN0(add_3_if_ge_5_11_out3), .OUT3(add_3_if_ge_5_2_out3), .OUT2(add_3_if_ge_5_2_out2),
    .OUT1(add_3_if_ge_5_2_out1), .OUT0(add_3_if_ge_5_2_out0));
  Add_3_if_GE_5 add_3_if_ge_5_3 (
    .IN3(1'b0), .IN2(add_3_if_ge_5_4_out3), .IN1(add_3_if_ge_5_15_out3), .IN0(add_3_if_ge_5_13_out3),
    .OUT3(add_3_if_ge_5_3_out3), .OUT2(add_3_if_ge_5_3_out2), .OUT1(add_3_if_ge_5_3_out1),
    .OUT0(add_3_if_ge_5_3_out0));
  Add_3_if_GE_5 add_3_if_ge_5_4 (
    .IN3(1'b0), .IN2(add_3_if_ge_5_23_out3), .IN1(add_3_if_ge_5_21_out3), .IN0(add_3_if_ge_5_19_out3),
    .OUT3(add_3_if_ge_5_4_out3), .OUT2(add_3_if_ge_5_4_out2), .OUT1(add_3_if_ge_5_4_out1),
    .OUT0(add_3_if_ge_5_4_out0));
  Add_3_if_GE_5 add_3_if_ge_5_5 (
    .IN3(add_3_if_ge_5_7_out2), .IN2(add_3_if_ge_5_7_out1), .IN1(add_3_if_ge_5_7_out0),
    .IN0(add_3_if_ge_5_8_out3), .OUT3(D4[0]), .OUT2(D3[3]), .OUT1(D3[2]), .OUT0(D3[1]));
  Add_3_if_GE_5 add_3_if_ge_5_6 (
    .IN3(add_3_if_ge_5_8_out2), .IN2(add_3_if_ge_5_8_out1), .IN1(add_3_if_ge_5_8_out0),
    .IN0(add_3_if_ge_5_30_out3), .OUT3(D3[0]), .OUT2(D2[3]), .OUT1(D2[2]), .OUT0(D2[1]));
  Add_3_if_GE_5 add_3_if_ge_5_7 (
    .IN3(add_3_if_ge_5_2_out2), .IN2(add_3_if_ge_5_2_out1), .IN1(add_3_if_ge_5_2_out0),
    .IN0(add_3_if_ge_5_9_out3), .OUT3(add_3_if_ge_5_7_out3), .OUT2(add_3_if_ge_5_7_out2),
    .OUT1(add_3_if_ge_5_7_out1), .OUT0(add_3_if_ge_5_7_out0));
  Add_3_if_GE_5 add_3_if_ge_5_8 (
    .IN3(add_3_if_ge_5_9_out2), .IN2(add_3_if_ge_5_9_out1), .IN1(add_3_if_ge_5_9_out0),
    .IN0(add_3_if_ge_5_10_out3), .OUT3(add_3_if_ge_5_8_out3), .OUT2(add_3_if_ge_5_8_out2),
    .OUT1(add_3_if_ge_5_8_out1), .OUT0(add_3_if_ge_5_8_out0));
  Add_3_if_GE_5 add_3_if_ge_5_9 (
    .IN3(add_3_if_ge_5_11_out2), .IN2(add_3_if_ge_5_11_out1), .IN1(add_3_if_ge_5_11_out0),
    .IN0(add_3_if_ge_5_12_out3), .OUT3(add_3_if_ge_5_9_out3), .OUT2(add_3_if_ge_5_9_out2),
    .OUT1(add_3_if_ge_5_9_out1), .OUT0(add_3_if_ge_5_9_out0));
  Add_3_if_GE_5 add_3_if_ge_5_10 (
    .IN3(add_3_if_ge_5_12_out2), .IN2(add_3_if_ge_5_12_out1), .IN1(add_3_if_ge_5_12_out0),
    .IN0(add_3_if_ge_5_33_out3), .OUT3(add_3_if_ge_5_10_out3), .OUT2(add_3_if_ge_5_10_out2),
    .OUT1(add_3_if_ge_5_10_out1), .OUT0(add_3_if_ge_5_10_out0));
  Add_3_if_GE_5 add_3_if_ge_5_11 (
    .IN3(add_3_if_ge_5_13_out2), .IN2(add_3_if_ge_5_13_out1), .IN1(add_3_if_ge_5_13_out0),
    .IN0(add_3_if_ge_5_14_out3), .OUT3(add_3_if_ge_5_11_out3), .OUT2(add_3_if_ge_5_11_out2),
    .OUT1(add_3_if_ge_5_11_out1), .OUT0(add_3_if_ge_5_11_out0));
  Add_3_if_GE_5 add_3_if_ge_5_12 (
    .IN3(add_3_if_ge_5_14_out2), .IN2(add_3_if_ge_5_14_out1), .IN1(add_3_if_ge_5_14_out0),
    .IN0(add_3_if_ge_5_34_out3), .OUT3(add_3_if_ge_5_12_out3), .OUT2(add_3_if_ge_5_12_out2),
    .OUT1(add_3_if_ge_5_12_out1), .OUT0(add_3_if_ge_5_12_out0));
  Add_3_if_GE_5 add_3_if_ge_5_13 (
    .IN3(add_3_if_ge_5_15_out2), .IN2(add_3_if_ge_5_15_out1), .IN1(add_3_if_ge_5_15_out0),
    .IN0(add_3_if_ge_5_16_out3), .OUT3(add_3_if_ge_5_13_out3), .OUT2(add_3_if_ge_5_13_out2),
    .OUT1(add_3_if_ge_5_13_out1), .OUT0(add_3_if_ge_5_13_out0));
  Add_3_if_GE_5 add_3_if_ge_5_14 (
    .IN3(add_3_if_ge_5_16_out2), .IN2(add_3_if_ge_5_16_out1), .IN1(add_3_if_ge_5_16_out0),
    .IN0(add_3_if_ge_5_35_out3), .OUT3(add_3_if_ge_5_14_out3), .OUT2(add_3_if_ge_5_14_out2),
    .OUT1(add_3_if_ge_5_14_out1), .OUT0(add_3_if_ge_5_14_out0));
  Add_3_if_GE_5 add_3_if_ge_5_15 (
    .IN3(add_3_if_ge_5_4_out2), .IN2(add_3_if_ge_5_4_out1), .IN1(add_3_if_ge_5_4_out0),
    .IN0(add_3_if_ge_5_17_out3), .OUT3(add_3_if_ge_5_15_out3), .OUT2(add_3_if_ge_5_15_out2),
    .OUT1(add_3_if_ge_5_15_out1), .OUT0(add_3_if_ge_5_15_out0));
  Add_3_if_GE_5 add_3_if_ge_5_16 (
    .IN3(add_3_if_ge_5_17_out2), .IN2(add_3_if_ge_5_17_out1), .IN1(add_3_if_ge_5_17_out0),
    .IN0(add_3_if_ge_5_18_out3), .OUT3(add_3_if_ge_5_16_out3), .OUT2(add_3_if_ge_5_16_out2),
    .OUT1(add_3_if_ge_5_16_out1), .OUT0(add_3_if_ge_5_16_out0));
  Add_3_if_GE_5 add_3_if_ge_5_17 (
    .IN3(add_3_if_ge_5_19_out2), .IN2(add_3_if_ge_5_19_out1), .IN1(add_3_if_ge_5_19_out0),
    .IN0(add_3_if_ge_5_20_out3), .OUT3(add_3_if_ge_5_17_out3), .OUT2(add_3_if_ge_5_17_out2),
    .OUT1(add_3_if_ge_5_17_out1), .OUT0(add_3_if_ge_5_17_out0));
  Add_3_if_GE_5 add_3_if_ge_5_18 (
    .IN3(add_3_if_ge_5_20_out2), .IN2(add_3_if_ge_5_20_out1), .IN1(add_3_if_ge_5_20_out0),
    .IN0(Binary_IN[7]), .OUT3(add_3_if_ge_5_18_out3), .OUT2(add_3_if_ge_5_18_out2),
    .OUT1(add_3_if_ge_5_18_out1), .OUT0(add_3_if_ge_5_18_out0));
  Add_3_if_GE_5 add_3_if_ge_5_19 (
    .IN3(add_3_if_ge_5_21_out2), .IN2(add_3_if_ge_5_21_out1), .IN1(add_3_if_ge_5_21_out0),
    .IN0(add_3_if_ge_5_22_out3), .OUT3(add_3_if_ge_5_19_out3), .OUT2(add_3_if_ge_5_19_out2),
    .OUT1(add_3_if_ge_5_19_out1), .OUT0(add_3_if_ge_5_19_out0));
  Add_3_if_GE_5 add_3_if_ge_5_20 (
    .IN3(add_3_if_ge_5_22_out2), .IN2(add_3_if_ge_5_22_out1), .IN1(add_3_if_ge_5_22_out0),
    .IN0(Binary_IN[8]), .OUT3(add_3_if_ge_5_20_out3), .OUT2(add_3_if_ge_5_20_out2),
    .OUT1(add_3_if_ge_5_20_out1), .OUT0(add_3_if_ge_5_20_out0));
  Add_3_if_GE_5 add_3_if_ge_5_21 (
    .IN3(add_3_if_ge_5_23_out2), .IN2(add_3_if_ge_5_23_out1), .IN1(add_3_if_ge_5_23_out0),
    .IN0(add_3_if_ge_5_24_out3), .OUT3(add_3_if_ge_5_21_out3), .OUT2(add_3_if_ge_5_21_out2),
    .OUT1(add_3_if_ge_5_21_out1), .OUT0(add_3_if_ge_5_21_out0));
  Add_3_if_GE_5 add_3_if_ge_5_22 (
    .IN3(add_3_if_ge_5_24_out2), .IN2(add_3_if_ge_5_24_out1), .IN1(add_3_if_ge_5_24_out0),
    .IN0(Binary_IN[9]), .OUT3(add_3_if_ge_5_22_out3), .OUT2(add_3_if_ge_5_22_out2),
    .OUT1(add_3_if_ge_5_22_out1), .OUT0(add_3_if_ge_5_22_out0));
  Add_3_if_GE_5 add_3_if_ge_5_23 (
    .IN3(1'b0), .IN2(add_3_if_ge_5_27_out3), .IN1(add_3_if_ge_5_26_out3), .IN0(add_3_if_ge_5_25_out3),
    .OUT3(add_3_if_ge_5_23_out3), .OUT2(add_3_if_ge_5_23_out2), .OUT1(add_3_if_ge_5_23_out1),
    .OUT0(add_3_if_ge_5_23_out0));
  Add_3_if_GE_5 add_3_if_ge_5_24 (
    .IN3(add_3_if_ge_5_25_out2), .IN2(add_3_if_ge_5_25_out1), .IN1(add_3_if_ge_5_25_out0),
    .IN0(Binary_IN[10]), .OUT3(add_3_if_ge_5_24_out3), .OUT2(add_3_if_ge_5_24_out2),
    .OUT1(add_3_if_ge_5_24_out1), .OUT0(add_3_if_ge_5_24_out0));
  Add_3_if_GE_5 add_3_if_ge_5_25 (
    .IN3(add_3_if_ge_5_26_out2), .IN2(add_3_if_ge_5_26_out1), .IN1(add_3_if_ge_5_26_out0),
    .IN0(Binary_IN[11]), .OUT3(add_3_if_ge_5_25_out3), .OUT2(add_3_if_ge_5_25_out2),
    .OUT1(add_3_if_ge_5_25_out1), .OUT0(add_3_if_ge_5_25_out0));
  Add_3_if_GE_5 add_3_if_ge_5_26 (
    .IN3(add_3_if_ge_5_27_out2), .IN2(add_3_if_ge_5_27_out1), .IN1(add_3_if_ge_5_27_out0),
    .IN0(Binary_IN[12]), .OUT3(add_3_if_ge_5_26_out3), .OUT2(add_3_if_ge_5_26_out2),
    .OUT1(add_3_if_ge_5_26_out1), .OUT0(add_3_if_ge_5_26_out0));
  Add_3_if_GE_5 add_3_if_ge_5_27 (
    .IN3(1'b0), .IN2(Binary_IN[15]), .IN1(Binary_IN[14]), .IN0(Binary_IN[13]), .OUT3(add_3_if_ge_5_27_out3),
    .OUT2(add_3_if_ge_5_27_out2), .OUT1(add_3_if_ge_5_27_out1), .OUT0(add_3_if_ge_5_27_out0));
  Add_3_if_GE_5 add_3_if_ge_5_28 (
    .IN3(add_3_if_ge_5_30_out2), .IN2(add_3_if_ge_5_30_out1), .IN1(add_3_if_ge_5_30_out0),
    .IN0(add_3_if_ge_5_31_out3), .OUT3(D2[0]), .OUT2(D1[3]), .OUT1(D1[2]), .OUT0(D1[1]));
  Add_3_if_GE_5 add_3_if_ge_5_29 (
    .IN3(add_3_if_ge_5_31_out2), .IN2(add_3_if_ge_5_31_out1), .IN1(add_3_if_ge_5_31_out0),
    .IN0(Binary_IN[1]), .OUT3(D1[0]), .OUT2(D0[3]), .OUT1(D0[2]), .OUT0(D0[1]));
  Add_3_if_GE_5 add_3_if_ge_5_30 (
    .IN3(add_3_if_ge_5_10_out2), .IN2(add_3_if_ge_5_10_out1), .IN1(add_3_if_ge_5_10_out0),
    .IN0(add_3_if_ge_5_32_out3), .OUT3(add_3_if_ge_5_30_out3), .OUT2(add_3_if_ge_5_30_out2),
    .OUT1(add_3_if_ge_5_30_out1), .OUT0(add_3_if_ge_5_30_out0));
  Add_3_if_GE_5 add_3_if_ge_5_31 (
    .IN3(add_3_if_ge_5_32_out2), .IN2(add_3_if_ge_5_32_out1), .IN1(add_3_if_ge_5_32_out0),
    .IN0(Binary_IN[2]), .OUT3(add_3_if_ge_5_31_out3), .OUT2(add_3_if_ge_5_31_out2),
    .OUT1(add_3_if_ge_5_31_out1), .OUT0(add_3_if_ge_5_31_out0));
  Add_3_if_GE_5 add_3_if_ge_5_32 (
    .IN3(add_3_if_ge_5_33_out2), .IN2(add_3_if_ge_5_33_out1), .IN1(add_3_if_ge_5_33_out0),
    .IN0(Binary_IN[3]), .OUT3(add_3_if_ge_5_32_out3), .OUT2(add_3_if_ge_5_32_out2),
    .OUT1(add_3_if_ge_5_32_out1), .OUT0(add_3_if_ge_5_32_out0));
  Add_3_if_GE_5 add_3_if_ge_5_33 (
    .IN3(add_3_if_ge_5_34_out2), .IN2(add_3_if_ge_5_34_out1), .IN1(add_3_if_ge_5_34_out0),
    .IN0(Binary_IN[4]), .OUT3(add_3_if_ge_5_33_out3), .OUT2(add_3_if_ge_5_33_out2),
    .OUT1(add_3_if_ge_5_33_out1), .OUT0(add_3_if_ge_5_33_out0));
  Add_3_if_GE_5 add_3_if_ge_5_34 (
    .IN3(add_3_if_ge_5_35_out2), .IN2(add_3_if_ge_5_35_out1), .IN1(add_3_if_ge_5_35_out0),
    .IN0(Binary_IN[5]), .OUT3(add_3_if_ge_5_34_out3), .OUT2(add_3_if_ge_5_34_out2),
    .OUT1(add_3_if_ge_5_34_out1), .OUT0(add_3_if_ge_5_34_out0));
  Add_3_if_GE_5 add_3_if_ge_5_35 (
    .IN3(add_3_if_ge_5_18_out2), .IN2(add_3_if_ge_5_18_out1), .IN1(add_3_if_ge_5_18_out0),
    .IN0(Binary_IN[6]), .OUT3(add_3_if_ge_5_35_out3), .OUT2(add_3_if_ge_5_35_out2),
    .OUT1(add_3_if_ge_5_35_out1), .OUT0(add_3_if_ge_5_35_out0));

  assign D0[0] = Binary_IN[0];
endmodule

module Add_3_if_GE_5 (
  input  IN3,
  input  IN2,
  input  IN1,
  input  IN0,
  output OUT3,
  output OUT2,
  output OUT1,
  output OUT0
);

  wire and_1_out, and_2_out, or_1_out;
  wire [3:0] adder_1_out;

  and and_1 (and_1_out, IN1, IN2);
  and and_2 (and_2_out, IN0, IN2);
  Adder #(.width(4)) adder_1 (.a({IN3, IN2, IN1, IN0}), .b(4'b0011), .out(adder_1_out), .cin(1'b0));  // open: cout
  Multiplexer #(.width(4)) multiplexer_1 (
    .in0({IN3, IN2, IN1, IN0}), .in1(adder_1_out), .out({OUT3, OUT2, OUT1, OUT0}), .sel(or_1_out));
  or or_1 (or_1_out, and_1_out, and_2_out, IN3);
endmodule

module SM (
  input  Reset,
  input  [7:0] Multiplier,
  input  Load,
  input  clk,
  input  [7:0] Multiplicand,
  output [15:0] Result,
  output Done
);

  wire not_1_out, shift_register_2_p22, shift_register_2_p23, shift_register_2_p24, shift_register_2_p25,
       shift_register_2_p26, shift_register_2_p27, shift_register_2_p28, shift_register_2_p29;
  wire [15:0] adder_1_out, multiplexer_1_out, multiplexer_2_out, register_1_q, shift_register_1_p14;

  // Shift_Register_part #(.length(16)) shift_register_1: pin names not known; wires that end beside it: Reset, Load, 1'b1, clk, 1'b0, Multiplier[0], Multiplier[1], Multiplier[2], Multiplier[3], Multiplier[4], Multiplier[5], Multiplier[6], Multiplier[7], shift_register_1_p14[0], shift_register_1_p14[1], shift_register_1_p14[2], shift_register_1_p14[3], shift_register_1_p14[4], shift_register_1_p14[5], shift_register_1_p14[6], shift_register_1_p14[7]
  // Shift_Register_part shift_register_2: pin names not known; wires that end beside it: Reset, Load, 1'b1, clk, 1'b0, Multiplicand[7], Multiplicand[6], Multiplicand[5], Multiplicand[4], Multiplicand[3], Multiplicand[2], Multiplicand[1], Multiplicand[0], 1'b0, 1'b0, 1'b0, 1'b0, 1'b0, 1'b0, 1'b0, 1'b0, shift_register_2_p22, shift_register_2_p23, shift_register_2_p24, shift_register_2_p25, shift_register_2_p26, shift_register_2_p27, shift_register_2_p28, shift_register_2_p29, shift_register_1_p14[8], shift_register_1_p14[9], shift_register_1_p14[10], shift_register_1_p14[11], shift_register_1_p14[12], shift_register_1_p14[13], shift_register_1_p14[14], shift_register_1_p14[15]
  nor nor_1 (Done, shift_register_2_p22, shift_register_2_p23, shift_register_2_p24, shift_register_2_p25, shift_register_2_p26, shift_register_2_p27, shift_register_2_p28, shift_register_2_p29);
  Multiplexer #(.width(16)) multiplexer_1 (
    .in0({16{1'b0}}), .in1(shift_register_1_p14), .out(multiplexer_1_out), .sel(shift_register_2_p29));
  Adder #(.width(16)) adder_1 (.a(multiplexer_1_out), .b(register_1_q), .out(adder_1_out), .cin(1'b0));  // open: cout
  Multiplexer #(.width(16)) multiplexer_2 (.in0(adder_1_out), .in1({16{1'b0}}), .out(multiplexer_2_out), .sel(Load));
  Register #(.width(16)) register_1 (.D(multiplexer_2_out), .en(not_1_out), .clk(clk), .Q(register_1_q), .clr(Reset));
  not not_1 (not_1_out, Done);
  Multiplexer #(.width(16)) multiplexer_3 (.in0({16{1'b0}}), .in1(register_1_q), .out(Result), .sel(Done));
endmodule

module BCD_7sd (
  input  [3:0] in_1,
  input  [3:0] in_2,
  input  [3:0] in_3,
  input  [3:0] in_4,
  input  [3:0] in_5,
  input  [3:0] in_6
);

  wire bcd_to_7_segment_decoder_1_p1, bcd_to_7_segment_decoder_2_p1, bcd_to_7_segment_decoder_2_p2,
       bcd_to_7_segment_decoder_2_p3, bcd_to_7_segment_decoder_2_p4, bcd_to_7_segment_decoder_2_p6,
       bcd_to_7_segment_decoder_2_p7, bcd_to_7_segment_decoder_2_p8, bcd_to_7_segment_decoder_3_p1,
       bcd_to_7_segment_decoder_3_p2, bcd_to_7_segment_decoder_3_p3, bcd_to_7_segment_decoder_3_p4,
       bcd_to_7_segment_decoder_3_p6, bcd_to_7_segment_decoder_3_p7, bcd_to_7_segment_decoder_3_p8,
       bcd_to_7_segment_decoder_4_p1, bcd_to_7_segment_decoder_4_p2, bcd_to_7_segment_decoder_4_p3,
       bcd_to_7_segment_decoder_4_p4, bcd_to_7_segment_decoder_4_p6, bcd_to_7_segment_decoder_4_p7,
       bcd_to_7_segment_decoder_4_p8, bcd_to_7_segment_decoder_5_p1, bcd_to_7_segment_decoder_5_p2,
       bcd_to_7_segment_decoder_5_p3, bcd_to_7_segment_decoder_5_p4, bcd_to_7_segment_decoder_5_p6,
       bcd_to_7_segment_decoder_5_p7, bcd_to_7_segment_decoder_5_p8, bcd_to_7_segment_decoder_6_p1,
       bcd_to_7_segment_decoder_6_p2, bcd_to_7_segment_decoder_6_p3, bcd_to_7_segment_decoder_6_p4,
       bcd_to_7_segment_decoder_6_p6, bcd_to_7_segment_decoder_6_p7, bcd_to_7_segment_decoder_6_p8,
       not_1_out, undriven;

  // BCD_to_7_Segment_decoder bcd_to_7_segment_decoder_1: pin names not known; wires that end beside it: bcd_to_7_segment_decoder_1_p1, in_2
  not not_1 (not_1_out, bcd_to_7_segment_decoder_1_p1);
  _7_Segment_Display u_7_segment_display_1 (.g(not_1_out), .dp(undriven));  // open: f, a, b, e, d, c
  // BCD_to_7_Segment_decoder bcd_to_7_segment_decoder_2: pin names not known; wires that end beside it: bcd_to_7_segment_decoder_2_p1, bcd_to_7_segment_decoder_2_p2, bcd_to_7_segment_decoder_2_p3, bcd_to_7_segment_decoder_2_p4, in_1, bcd_to_7_segment_decoder_2_p6, bcd_to_7_segment_decoder_2_p7, bcd_to_7_segment_decoder_2_p8
  _7_Segment_Display u_7_segment_display_2 (
    .g(bcd_to_7_segment_decoder_2_p1), .f(bcd_to_7_segment_decoder_2_p3), .a(bcd_to_7_segment_decoder_2_p6),
    .b(bcd_to_7_segment_decoder_2_p8), .e(bcd_to_7_segment_decoder_2_p2), .d(bcd_to_7_segment_decoder_2_p4),
    .c(bcd_to_7_segment_decoder_2_p7), .dp(undriven));
  // BCD_to_7_Segment_decoder bcd_to_7_segment_decoder_3: pin names not known; wires that end beside it: bcd_to_7_segment_decoder_3_p1, bcd_to_7_segment_decoder_3_p2, bcd_to_7_segment_decoder_3_p3, bcd_to_7_segment_decoder_3_p4, in_3, bcd_to_7_segment_decoder_3_p6, bcd_to_7_segment_decoder_3_p7, bcd_to_7_segment_decoder_3_p8
  _7_Segment_Display u_7_segment_display_3 (
    .g(bcd_to_7_segment_decoder_3_p1), .f(bcd_to_7_segment_decoder_3_p3), .a(bcd_to_7_segment_decoder_3_p6),
    .b(bcd_to_7_segment_decoder_3_p8), .e(bcd_to_7_segment_decoder_3_p2), .d(bcd_to_7_segment_decoder_3_p4),
    .c(bcd_to_7_segment_decoder_3_p7), .dp(undriven));
  // BCD_to_7_Segment_decoder bcd_to_7_segment_decoder_4: pin names not known; wires that end beside it: bcd_to_7_segment_decoder_4_p1, bcd_to_7_segment_decoder_4_p2, bcd_to_7_segment_decoder_4_p3, bcd_to_7_segment_decoder_4_p4, in_4, bcd_to_7_segment_decoder_4_p6, bcd_to_7_segment_decoder_4_p7, bcd_to_7_segment_decoder_4_p8
  _7_Segment_Display u_7_segment_display_4 (
    .g(bcd_to_7_segment_decoder_4_p1), .f(bcd_to_7_segment_decoder_4_p3), .a(bcd_to_7_segment_decoder_4_p6),
    .b(bcd_to_7_segment_decoder_4_p8), .e(bcd_to_7_segment_decoder_4_p2), .d(bcd_to_7_segment_decoder_4_p4),
    .c(bcd_to_7_segment_decoder_4_p7), .dp(undriven));
  // BCD_to_7_Segment_decoder bcd_to_7_segment_decoder_5: pin names not known; wires that end beside it: bcd_to_7_segment_decoder_5_p1, bcd_to_7_segment_decoder_5_p2, bcd_to_7_segment_decoder_5_p3, bcd_to_7_segment_decoder_5_p4, in_5, bcd_to_7_segment_decoder_5_p6, bcd_to_7_segment_decoder_5_p7, bcd_to_7_segment_decoder_5_p8
  _7_Segment_Display u_7_segment_display_5 (
    .g(bcd_to_7_segment_decoder_5_p1), .f(bcd_to_7_segment_decoder_5_p3), .a(bcd_to_7_segment_decoder_5_p6),
    .b(bcd_to_7_segment_decoder_5_p8), .e(bcd_to_7_segment_decoder_5_p2), .d(bcd_to_7_segment_decoder_5_p4),
    .c(bcd_to_7_segment_decoder_5_p7), .dp(undriven));
  // BCD_to_7_Segment_decoder bcd_to_7_segment_decoder_6: pin names not known; wires that end beside it: bcd_to_7_segment_decoder_6_p1, bcd_to_7_segment_decoder_6_p2, bcd_to_7_segment_decoder_6_p3, bcd_to_7_segment_decoder_6_p4, in_6, bcd_to_7_segment_decoder_6_p6, bcd_to_7_segment_decoder_6_p7, bcd_to_7_segment_decoder_6_p8
  _7_Segment_Display u_7_segment_display_6 (
    .g(bcd_to_7_segment_decoder_6_p1), .f(bcd_to_7_segment_decoder_6_p3), .a(bcd_to_7_segment_decoder_6_p6),
    .b(bcd_to_7_segment_decoder_6_p8), .e(bcd_to_7_segment_decoder_6_p2), .d(bcd_to_7_segment_decoder_6_p4),
    .c(bcd_to_7_segment_decoder_6_p7), .dp(undriven));
endmodule

module Shift_Register (
  input  BTNR,
  input  Reset,
  input  [3:0] D4,
  input  [3:0] D3,
  input  [3:0] D2,
  input  [3:0] D1,
  input  [3:0] D0,
  input  BTNL,
  input  clk,
  output [3:0] O2,
  output [3:0] O1,
  output [3:0] O0
);

  wire and_1_out, and_2_out, decoder_1_out0, decoder_2_out2, not_1_out, not_2_out;
  wire [1:0] adder_1_out, adder_2_out, multiplexer_1_out, multiplexer_2_out, multiplexer_3_out, register_1_q;

  Decoder #(.select(2)) decoder_1 (.out0(decoder_1_out0), .sel(register_1_q));  // open: out1, out2, out3, en
  and and_1 (and_1_out, BTNR, not_1_out);
  not not_1 (not_1_out, decoder_1_out0);
  Adder #(.width(2)) adder_1 (.a(2'b11), .b(register_1_q), .out(adder_1_out));  // open: cin, cout
  Multiplexer #(.width(2)) multiplexer_1 (
    .in0(register_1_q), .in1(adder_1_out), .out(multiplexer_1_out), .sel(and_1_out));
  Adder #(.width(2)) adder_2 (.a(2'b01), .b(register_1_q), .out(adder_2_out));  // open: cin, cout
  Multiplexer #(.select(2), .width(2)) multiplexer_2 (
    .in0(register_1_q), .in1(multiplexer_3_out), .in2(multiplexer_1_out), .in3(register_1_q),
    .out(multiplexer_2_out), .sel({BTNR, BTNL}));
  Multiplexer #(.width(2)) multiplexer_3 (
    .in0(register_1_q), .in1(adder_2_out), .out(multiplexer_3_out), .sel(and_2_out));
  Register #(.width(2)) register_1 (.D(multiplexer_2_out), .clk(clk), .Q(register_1_q), .clr(Reset));  // open: en
  not not_2 (not_2_out, decoder_2_out2);
  and and_2 (and_2_out, not_2_out, BTNL);
  Decoder #(.select(2)) decoder_2 (.out2(decoder_2_out2), .sel(register_1_q));  // open: out0, out1, out3, en
  Multiplexer #(.select(2), .width(4)) multiplexer_4 (
    .in0(D2), .in1(D3), .in2(D4), .out(O2), .sel(register_1_q));  // open: in3
  Multiplexer #(.select(2), .width(4)) multiplexer_5 (
    .in0(D1), .in1(D2), .in2(D3), .out(O1), .sel(register_1_q));  // open: in3
  Multiplexer #(.select(2), .width(4)) multiplexer_6 (
    .in0(D0), .in1(D1), .in2(D2), .out(O0), .sel(register_1_q));  // open: in3
endmodule

module Driver_7sd (
  input  BTNR,
  input  [3:0] Sign,
  input  Reset,
  input  [3:0] D4,
  input  [3:0] D3,
  input  [3:0] D2,
  input  [3:0] D1,
  input  [3:0] D0,
  input  BTNL
);

  wire and_1_out, and_2_out, bcd_to_7_segment_decoder_1_p1, bcd_to_7_segment_decoder_2_p1,
       bcd_to_7_segment_decoder_2_p2, bcd_to_7_segment_decoder_2_p3, bcd_to_7_segment_decoder_2_p4,
       bcd_to_7_segment_decoder_2_p6, bcd_to_7_segment_decoder_2_p7, bcd_to_7_segment_decoder_2_p8,
       bcd_to_7_segment_decoder_3_p1, bcd_to_7_segment_decoder_3_p2, bcd_to_7_segment_decoder_3_p3,
       bcd_to_7_segment_decoder_3_p4, bcd_to_7_segment_decoder_3_p6, bcd_to_7_segment_decoder_3_p7,
       bcd_to_7_segment_decoder_3_p8, bcd_to_7_segment_decoder_4_p1, bcd_to_7_segment_decoder_4_p2,
       bcd_to_7_segment_decoder_4_p3, bcd_to_7_segment_decoder_4_p4, bcd_to_7_segment_decoder_4_p6,
       bcd_to_7_segment_decoder_4_p7, bcd_to_7_segment_decoder_4_p8, clock_1_out, decoder_1_out0,
       decoder_2_out2, not_1_out, not_2_out, not_3_out, undriven;
  wire [1:0] adder_1_out, adder_2_out, multiplexer_1_out, multiplexer_2_out, multiplexer_3_out, register_1_q;
  wire [3:0] bcd_to_7_segment_decoder_2_p5, bcd_to_7_segment_decoder_3_p5, bcd_to_7_segment_decoder_4_p5;

  Decoder #(.select(2)) decoder_1 (.out0(decoder_1_out0), .sel(register_1_q));  // open: out1, out2, out3, en
  Clock clock_1 (.out(clock_1_out));
  and and_1 (and_1_out, BTNR, not_1_out);
  not not_1 (not_1_out, decoder_1_out0);
  Adder #(.width(2)) adder_1 (.a(2'b11), .b(register_1_q), .out(adder_1_out));  // open: cin, cout
  Multiplexer #(.width(2)) multiplexer_1 (
    .in0(register_1_q), .in1(adder_1_out), .out(multiplexer_1_out), .sel(and_1_out));
  Adder #(.width(2)) adder_2 (.a(2'b01), .b(register_1_q), .out(adder_2_out));  // open: cin, cout
  Multiplexer #(.select(2), .width(2)) multiplexer_2 (
    .in0(register_1_q), .in1(multiplexer_3_out), .in2(multiplexer_1_out), .in3(register_1_q),
    .out(multiplexer_2_out), .sel({BTNR, BTNL}));
  Multiplexer #(.width(2)) multiplexer_3 (
    .in0(register_1_q), .in1(adder_2_out), .out(multiplexer_3_out), .sel(and_2_out));
  // BCD_to_7_Segment_decoder bcd_to_7_segment_decoder_1: pin names not known; wires that end beside it: bcd_to_7_segment_decoder_1_p1, Sign
  Register #(.width(2)) register_1 (
    .D(multiplexer_2_out), .clk(clock_1_out), .Q(register_1_q), .clr(Reset));  // open: en
  not not_2 (not_2_out, decoder_2_out2);
  and and_2 (and_2_out, not_2_out, BTNL);
  not not_3 (not_3_out, bcd_to_7_segment_decoder_1_p1);
  _7_Segment_Display u_7_segment_display_1 (.g(not_3_out), .dp(undriven));  // open: f, a, b, e, d, c
  Decoder #(.select(2)) decoder_2 (.out2(decoder_2_out2), .sel(register_1_q));  // open: out0, out1, out3, en
  // BCD_to_7_Segment_decoder bcd_to_7_segment_decoder_2: pin names not known; wires that end beside it: bcd_to_7_segment_decoder_2_p1, bcd_to_7_segment_decoder_2_p2, bcd_to_7_segment_decoder_2_p3, bcd_to_7_segment_decoder_2_p4, bcd_to_7_segment_decoder_2_p5, bcd_to_7_segment_decoder_2_p6, bcd_to_7_segment_decoder_2_p7, bcd_to_7_segment_decoder_2_p8
  Multiplexer #(.select(2), .width(4)) multiplexer_4 (
    .in0(D2), .in1(D3), .in2(D4), .out(bcd_to_7_segment_decoder_2_p5), .sel(register_1_q));  // open: in3
  _7_Segment_Display u_7_segment_display_2 (
    .g(bcd_to_7_segment_decoder_2_p1), .f(bcd_to_7_segment_decoder_2_p3), .a(bcd_to_7_segment_decoder_2_p6),
    .b(bcd_to_7_segment_decoder_2_p8), .e(bcd_to_7_segment_decoder_2_p2), .d(bcd_to_7_segment_decoder_2_p4),
    .c(bcd_to_7_segment_decoder_2_p7), .dp(undriven));
  // BCD_to_7_Segment_decoder bcd_to_7_segment_decoder_3: pin names not known; wires that end beside it: bcd_to_7_segment_decoder_3_p1, bcd_to_7_segment_decoder_3_p2, bcd_to_7_segment_decoder_3_p3, bcd_to_7_segment_decoder_3_p4, bcd_to_7_segment_decoder_3_p5, bcd_to_7_segment_decoder_3_p6, bcd_to_7_segment_decoder_3_p7, bcd_to_7_segment_decoder_3_p8
  Multiplexer #(.select(2), .width(4)) multiplexer_5 (
    .in0(D1), .in1(D2), .in2(D3), .out(bcd_to_7_segment_decoder_3_p5), .sel(register_1_q));  // open: in3
  _7_Segment_Display u_7_segment_display_3 (
    .g(bcd_to_7_segment_decoder_3_p1), .f(bcd_to_7_segment_decoder_3_p3), .a(bcd_to_7_segment_decoder_3_p6),
    .b(bcd_to_7_segment_decoder_3_p8), .e(bcd_to_7_segment_decoder_3_p2), .d(bcd_to_7_segment_decoder_3_p4),
    .c(bcd_to_7_segment_decoder_3_p7), .dp(undriven));
  // BCD_to_7_Segment_decoder bcd_to_7_segment_decoder_4: pin names not known; wires that end beside it: bcd_to_7_segment_decoder_4_p1, bcd_to_7_segment_decoder_4_p2, bcd_to_7_segment_decoder_4_p3, bcd_to_7_segment_decoder_4_p4, bcd_to_7_segment_decoder_4_p5, bcd_to_7_segment_decoder_4_p6, bcd_to_7_segment_decoder_4_p7, bcd_to_7_segment_decoder_4_p8
  _7_Segment_Display u_7_segment_display_4 (
    .g(bcd_to_7_segment_decoder_4_p1), .f(bcd_to_7_segment_decoder_4_p3), .a(bcd_to_7_segment_decoder_4_p6),
    .b(bcd_to_7_segment_decoder_4_p8), .e(bcd_to_7_segment_decoder_4_p2), .d(bcd_to_7_segment_decoder_4_p4),
    .c(bcd_to_7_segment_decoder_4_p7), .dp(undriven));
  Multiplexer #(.select(2), .width(4)) multiplexer_6 (
    .in0(D0), .in1(D1), .in2(D2), .out(bcd_to_7_segment_decoder_4_p5), .sel(register_1_q));  // open: in3
endmodule
